# Fritzing sketch fritzingdesign (saved by Fritzing 0.9.3b)
circuit board: 8.46667cm x 5.64444cm
breadboards: 1

parts:
  LED1 = smd LED [color="Red (633nm)" package="0603 [SMD]"]
  J1 = Piezo Speaker
  S1 = SWITCH-MOMENTARY-2 [package=tactile-pth]
  R1 = Resistor [tolerance=±5% resistance=220 package=THT]
  PCB2 = RTC_DS1302_module
  U1 = ESP32-38PinWide [part_number=ESP32-38PinWide]
  Composant2 = YX 5300 Serial MP3 Player

nets (from the schematic view):
  GND: LED1.cathode, J1.pin1, S1.1, PCB2.GND, U1.GND, Composant2.GND
  N1: LED1.anode, R1.Pin_0
  N2: J1.pin2, U1.GPIO25
  N3: S1.2, U1.GPIO14
  N4: R1.Pin_1, U1.GPIO33
  VCC: PCB2.VCC, U1.3.3, Composant2.VCC
  N5: PCB2.RST, U1.GPIO5
  N6: PCB2.DAT, U1.GPIO18
  N7: PCB2.CLK, U1.GPIO19
  N8: U1.GPIO16, Composant2.TXD
  N9: U1.GPIO17, Composant2.RXD

custom parts:
  RTC_DS1302_module: Arduino module DS1302 SPI Real Time Clock
  ESP32-38PinWide: Generic 38-Pin ESP32 with wide format (only access to one side of pins on a breadboard) based on Stephen Lilley's HiLetgo ESP-WROOM-32 ESP32 ESP-32S Development Board.
